# Fritzing sketch schema_1 (saved by Fritzing 0.8.7b)
breadboards: 1

parts:
  Onderdeel1 = Arduino Uno (Rev3)
  LED1 = RGB LED (com. anode, rbg) [package="5 mm [THT]"]
  R1 = Resistor [tolerance=±5% resistance=470 package=THT]
  R2 = Resistor [tolerance=±5% resistance=470 package=THT]
  R3 = Resistor [tolerance=±5% resistance=470 package=THT]
  R4 = Resistor [tolerance=±5% resistance=10k package=THT]
  S1 = Pushbutton [package="[THT]"]
  R5 = Resistor [tolerance=±5% resistance=10k package=THT]
  S2 = Pushbutton [package="[THT]"]

nets:
  N1: Onderdeel1.D9_PWM, R1.Pin_1
  N2: Onderdeel1.D10_PWM/SS, R2.Pin_1
  N3: Onderdeel1.D11_PWM/MOSI, R3.Pin_1
  N4: Onderdeel1.D2, R5.Pin_1, S2.Pin_3, S2.Pin_4
  N5: Onderdeel1.D3_PWM, R4.Pin_1, S1.Pin_3, S1.Pin_4
  N6: Onderdeel1.5V, LED1.common_anode, S1.Pin_1, S1.Pin_2, R5.Pin_0, S2.Pin_1, S2.Pin_2
  N7: Onderdeel1.GND, R4.Pin_0
  N8: LED1.red_cathode, R1.Pin_0
  N9: LED1.blue_cathode, R2.Pin_0
  N10: LED1.green_cathode, R3.Pin_0
